// Logisim project Circuitos P2.circ as structural Verilog: 1 circuit, main circuit main
module main (
  input  A,
  input  B,
  output X,
  output X_2,
  output X_3,
  output X_4,
  output X_5
);

  wire and_1_out, and_2_out, not_1_out, not_2_out, not_3_out, or_1_out, or_2_out;

  not not_1 (not_1_out, A);
  and and_1 (and_1_out, A, B);
  or or_1 (or_1_out, A, B);
  and and_2 (and_2_out, A, B);
  or or_2 (or_2_out, A, B);
  not not_2 (not_2_out, and_1_out);
  not not_3 (not_3_out, or_1_out);
  not not_4 (X, not_1_out);
  not not_5 (X_2, not_2_out);
  not not_6 (X_3, not_3_out);
  not not_7 (X_4, and_2_out);
  not not_8 (X_5, or_2_out);
endmodule
